# Fritzing sketch Oximeter Sketch (saved by Fritzing 0.9.5d)
breadboards: 1

parts:
  Part1 = Arduino Nano (Rev3.0)
  M1 = MAX30102
  OLED_I2C1 = OLED 128x64 I2C Monochrome Display
  S1 = Pushbutton [package="[SMD]"]

nets:
  GND: Part1.GND, M1.GND, OLED_I2C1.GND, S1.Pin_1, S1.Pin_2
  N1: Part1.D3, S1.Pin_3, S1.Pin_4
  5V: Part1.5V, M1.VIN, OLED_I2C1.VDD
  N2: Part1.A5, M1.SCL, OLED_I2C1.SCK
  N3: Part1.A4, M1.SDA, OLED_I2C1.SDA

custom parts:
  MAX30102: Oximeter module using the MAX30102 chip. You may wish to read (and check your module) this post on power problems with these modules: https://reedpaper.wordpress.com/2018/08/22/pulse-oximeter-max30100-max30102-how-to-fix-wrong-board/ . As usual, if you want the mounting holes in pcb, you need to drag a hole over the pad in silkscreen to actually drill the hole (by default they are not drilled)
